# Fritzing sketch Wiring Diagram Climate Light (saved by Fritzing 1.0.5)
breadboards: 1

parts:
  Mod1 = Amica NodeMCU DEVKIT 1.0
  U1 = Module 4 Relais 5V [package="Module 4 Relais 5V"]
  LCM1602_IIC1 = LCM1602 IIC [part_number="LCM1602 IIC" chip_label="LCM1602 IIC" package="DIP (Dual Inline) [THT]"]
  LCD2 = LCD screen
  J1 = Piezo Speaker
  LED4 = LED - 3mm [color="Red (633nm)" current=0.030A package="3 mm [THT]"]
  DHT1 = Humidity and Temperature Sensor DHT11
  Mod2 = MQ-7 breakout
  S1 = KY-026
  Part3 = Lilypad Battery Connect
  LED5 = LEDs [package=led10mm]

nets:
  N1: Mod1.pin1, Mod1.pin_10, Mod1.pin_26, DHT1.Vcc, S1.pin1
  GND: Mod1.pin2, Mod1.pin_9, Mod1.pin_25, Mod1.pin_29, U1.GND, LCM1602_IIC1.GND, DHT1.Data-signal, S1.pin2
  N2: Mod1.pin5, S1.pin4
  N3: Mod1.pin6, DHT1.GND_1
  N4: Mod1.pin7, U1.IN2
  N5: Mod1.pin8, U1.IN1
  N6: Mod1.pin_11, LED4.anode
  N7: Mod1.pin_12, J1.pin2
  N8: Mod1.pin_13, LCM1602_IIC1.SDA
  N9: Mod1.pin_14, LCM1602_IIC1.SCL
  N10: Mod1.pin_16, Mod2.AO
  VCC: Mod1.pin_30, U1.VCC, LCM1602_IIC1.VCC
  N11: U1.K4-NF, Part3.+
  N12: U1.K3-Com, U1.K4-Com
  N13: U1.K3-NO, LED5.C
  VSS: LCM1602_IIC1.VSS, LCD2.VSS
  VDD: LCM1602_IIC1.VDD, LCD2.VDD
  N14: LCM1602_IIC1.V0, LCD2.V0
  N15: LCM1602_IIC1.RS, LCD2.RS
  N16: LCM1602_IIC1.RW, LCD2.R/W
  N17: LCM1602_IIC1.E, LCD2.E
  N18: LCM1602_IIC1.D0, LCD2.DB0
  N19: LCM1602_IIC1.D1, LCD2.DB1
  N20: LCM1602_IIC1.D2, LCD2.DB2
  N21: LCM1602_IIC1.D3, LCD2.DB3
  N22: LCM1602_IIC1.D4, LCD2.DB4
  N23: LCM1602_IIC1.D5, LCD2.DB5
  N24: LCM1602_IIC1.D6, LCD2.DB6
  N25: LCM1602_IIC1.D7, LCD2.DB7
  N26: LCM1602_IIC1.A, LCD2.LED+
  N27: LCM1602_IIC1.K, LCD2.LED-
  N28: LCM1602_IIC1.LED_A, LCM1602_IIC1.LED_B
  N29: J1.pin1, LED4.cathode, Mod2.GND

notes:
  240V AC power eksternal
  MQ2 Gas Sensor
  DHT 11 Sensor Suhu dan Kelembapan
  Flame Sensor
  LCD 1602 I2C
  Relay 4 Channel
  Lampu 3 Watt
  Buzzer
  Netral

custom parts:
  Module 4 Relais 5V: Module 4 Relais 5V 4x SPD-06VDC-SD-C
  LCM1602 IIC: I2C-Module to use a 1602 or 2004 LCD on with the wire.h libory Serial LCD Modul
  Humidity and Temperature Sensor DHT11: Digital relative humidity & temperature sensor DHT11
  MQ-7 breakout: MQ-5 gas sensor
  KY-026: ky-026 flame sensor module
  LEDs: LEDs Standard schematic elements and footprints for 5mm, 3mm, 1206, and 0603 sized LEDs. 5mm - Spark Fun Electronics SKU : COM-00529 (and others)

// code stored in the sketch: Untitled3.ino
#include <DHT.h>
#include <Wire.h>
#include <LiquidCrystal_I2C.h>

#define DHTPIN D5         // pin data DHT22
#define DHTTYPE DHT22

#define MQ2PIN A0         // pin analog MQ-2
#define LED1 D6           // LED indikator 1
#define LED2 D7           // LED indikator 2
#define BUZZER D8         // Buzzer
#define RELAY D1          // Relay kontrol lampu

DHT dht(DHTPIN, DHTTYPE);
LiquidCrystal_I2C lcd(0x27, 16, 2); // Alamat I2C bisa beda (0x27 atau 0x3F)

void setup() {
  Serial.begin(9600);
  dht.begin();
  lcd.begin();
  lcd.backlight();

  pinMode(LED1, OUTPUT);
  pinMode(LED2, OUTPUT);
  pinMode(BUZZER, OUTPUT);
  pinMode(RELAY, OUTPUT);
  digitalWrite(RELAY, HIGH); // Relay mati awalnya

  lcd.setCursor(0, 0);
  lcd.print("Monitoring...");
}

void loop() {
  float temp = dht.readTemperature();
  float hum = dht.readHumidity();
  int gasValue = analogRead(MQ2PIN); // nilai 0?1023

  // Tampilkan ke Serial Monitor
  Serial.print("Temp: "); Serial.print(temp);
  Serial.print("  Hum: "); Serial.print(hum);
  Serial.print("  Gas: "); Serial.println(gasValue);

  // Tampilkan ke LCD
  lcd.setCursor(0, 0);
  lcd.print("T:"); lcd.print(temp); lcd.print((char)223); lcd.print("C ");
  lcd.print("H:"); lcd.print(hum); lcd.print("%");

  lcd.setCursor(0, 1);
  lcd.print("Gas: "); lcd.print(gasValue);
  lcd.print("        "); // bersihkan sisa teks lama

  // Logika peringatan
  if (gasValue > 400) {
    digitalWrite(LED1, HIGH);
    digitalWrite(BUZZER, HIGH);
    digitalWrite(RELAY, LOW); // Relay aktif (lampu nyala)
  } else {
    digitalWrite(LED1, LOW);
    digitalWrite(BUZZER, LOW);
    digitalWrite(RELAY, HIGH); // Relay mati (lampu mati)
  }

  // Indikator suhu tinggi
  if (temp > 35) {
    digitalWrite(LED2, HIGH);
  } else {
    digitalWrite(LED2, LOW);
  }

  delay(2000);
}
